# Fritzing sketch hardware (saved by Fritzing 0.8.3b)
circuit board: 7.65756cm x 4.81466cm
breadboards: 1

parts:
  J8 = shrouded pin header, 10 pins [form="♂ (shrouded male)"]
  R2 = Resistor [tolerance=±5% resistance=330 package=THT]
  LED4 = LED - 5mm [color="Red (633nm)" package="5 mm [THT]"]
  J3 = female pin header, 10 pins [form="♀ (female)"]
  C7 = Ceramic Capacitor [capacitance=100nF package="100 mil [THT, multilayer]"]
  C3 = Ceramic Capacitor [capacitance=100nF package="100 mil [THT, multilayer]"]
  L1 = LM35 Temperature Sensor [package="TO92 [THT]"]
  LED2 = LED - 5mm [color="Orange (620nm)" package="5 mm [THT]"]
  J7 = female pin header, 2 pins [form="♀ (female)"]
  C1 = Ceramic Capacitor [capacitance=100nF package="100 mil [THT, multilayer]"]
  X2 = DB9 Connector [package=db9]
  J1 = female pin header, 20 pins [form="♀ (female)"]
  C5 = Ceramic Capacitor [capacitance=100nF package="200 mil [THT, multilayer]"]
  J2 = female pin header, 20 pins [form="♀ (female)"]
  R1 = Resistor [tolerance=±5% resistance=330 package=THT]
  J4 = female pin header, 10 pins [form="♀ (female)"]
  LED3 = LED - 5mm [color="Green (560nm)" package="5 mm [THT]"]
  J5 = female pin header, 8 pins [form="♀ (female)"]
  LED1 = LED - 5mm [color="Yellow (595nm)" package="5 mm [THT]"]
  C2 = Ceramic Capacitor [capacitance=100nF package="100 mil [THT, multilayer]"]
  C4 = Ceramic Capacitor [capacitance=100nF package="100 mil [THT, multilayer]"]
  C6 = Ceramic Capacitor [capacitance=100nF package="100 mil [THT, multilayer]"]
  J6 = female pin header, 8 pins [form="♀ (female)"]

nets:
  N1: J8.pin1, J2.pin17
  N2: J8.pin2, J2.pin15
  N3: J8.pin3, J2.pin16
  N4: J8.pin5, J2.pin14
  N5: J8.pin6, J8.pin10, R2.Pin_1, C7.1, L1.+Vs, LED2.cathode, J7.pin2, C1.0, X2.5, J1.pin11, J2.pin10, R1.Pin_0, J4.pin10, LED1.cathode, C2.1, C4.0, C6.1, J6.pin7
  N6: J8.pin8, J1.pin9
  N7: J8.pin9, LED4.anode, J7.pin1, C1.1, J1.pin10, J2.pin11, J4.pin1, C2.0, C4.1, J6.pin8
  N8: R2.Pin_0, LED4.cathode
  N9: J3.pin6, LED1.anode
  N10: J3.pin8, LED2.anode
  N11: C7.0, J5.pin7
  N12: C3.0, J5.pin4
  N13: C3.1, J5.pin5
  N14: L1.Vout, J2.pin8
  N15: L1.GND, J2.pin1
  N16: X2.2, J6.pin6
  N17: X2.3, J6.pin5
  N18: J1.pin1, LED3.anode
  N19: J1.pin14, J4.pin2
  N20: J1.pin15, J4.pin3
  N21: J1.pin16, J6.pin4
  N22: J1.pin17, J6.pin3
  N23: J1.pin18, J4.pin9
  N24: C5.0, J5.pin6
  N25: C5.1, J5.pin8
  N26: R1.Pin_1, LED3.cathode
  N27: J5.pin3, C6.0
